# Fritzing sketch SchémaAnémoEsp32 (saved by Fritzing 0.9.3b)
breadboards: 1

parts:
  R1 = Resistor [tolerance=±5% resistance=100 package=THT]
  R2 = Resistor [tolerance=±5% resistance=100 package=THT]
  D1 = Rectifier Diode [part_number=1N4148 package="300 mil [THT]"]
  R3 = Resistor [tolerance=±5% resistance=10k package=THT]
  Optocoupleur = TLP621 [part_number=PC817 package=THT]
  Connecteur_anémomètre = Camdenboss CTB0158-4 [part_number=CTB0158-4 package=THT]

nets:
  N1: R1.Pin_0, Connecteur_anémomètre.pin3
  N2: R1.Pin_1, D1.cathode, Optocoupleur.Pin_1
  N3: R2.Pin_0, Connecteur_anémomètre.pin2
  N4: R2.Pin_1, D1.anode, Optocoupleur.Pin_2
  3.3V/Vers ESP32 (GPIO 02): R3.Pin_0, R3.Pin_1, Optocoupleur.Pin_4
  GND: Optocoupleur.Pin_3, Connecteur_anémomètre.pin1
  12V: Connecteur_anémomètre.pin4

notes:
  Rouge (Alim +)
  jaune (NMEA+)
  Vert (NMEA+)
  Bleu (Alim-)
